# Fritzing sketch Photo Interrupter (saved by Fritzing 0.9.2b)
breadboards: 1

parts:
  Part1 = Arduino Uno (Rev3) - ICSP
  U1 = GP1A57HR [package=gp1a57hr]
  R1 = Resistor [tolerance=±5% resistance=220 package="2010 [SMD]"]
  LED1 = LED - 5mm [color="Red (633nm)" package="5 mm [THT]"]
  R2 = Resistor [tolerance=±5% resistance=220 package="2010 [SMD]"]

nets:
  N1: Part1.D9_PWM, R2.Pin_1
  N2: Part1.GND, U1.1, U1.4
  N3: Part1.D2, U1.2
  N4: Part1.5V, U1.3, R1.Pin_0
  N5: U1.5, R1.Pin_1
  N6: LED1.cathode, R2.Pin_0
